// Logisim project PD0.circ as structural Verilog: 1 circuit, main circuit main
module main (
  input  [3:0] in_1,
  output out_2
);

  wire i0_out, i1_out, i2_out, i3_out;

  // Probe on in_1
  or i0 (i0_out, in_1[1], in_1[3]);
  or i1 (i1_out, ~in_1[3], ~in_1[1]);  // OR_Gate
  or i2 (i2_out, ~in_1[1], in_1[2], in_1[0]);  // OR_Gate
  or i3 (i3_out, in_1[2], in_1[1], in_1[0]);
  and F_x (out_2, i0_out, i1_out, i2_out, i3_out);

  // Other names for the same wires on the sheet: X0 = in_1[0]; X1 = in_1[1]; X2 = in_1[2]; X3 = in_1[3];
  //   OUTPUT = out_2

  // Notes on the sheet:
  //   Funcion
  //   Input
  //   Output
endmodule
