// Logisim project PD1.circ as structural Verilog: 5 circuits, main circuit main
module main (
  input  [3:0] in_1,
  input  [3:0] in_2,
  input  [3:0] in_3,
  output [5:0] out_4
);

  wire comparador_ca2_1_out_3;
  wire [5:0] A, adder_1_out, adder_2_out, adder_3_out, B, C, minus_C, multiplicar_x2_1_out_2;

  Conversor_4_a_6 conversor_4_a_6_1 (.in_1(in_1), .out_2(A));
  Conversor_4_a_6 conversor_4_a_6_2 (.in_1(in_2), .out_2(B));
  Conversor_4_a_6 conversor_4_a_6_3 (.in_1(in_3), .out_2(C));
  Conversor_a_Negativo conversor_a_negativo_1 (.in_1(C), .out_2(minus_C));
  Adder #(.width(6)) adder_1 (.a(A), .b(minus_C), .out(adder_1_out));  // open: cin, cout
  Adder #(.width(6)) adder_2 (.a(B), .b(minus_C), .out(adder_2_out));  // open: cin, cout
  Adder #(.width(6)) adder_3 (.a(B), .b(C), .out(adder_3_out));  // open: cin, cout
  Multiplicar_x2 multiplicar_x2_1 (.in_1(adder_2_out), .out_2(multiplicar_x2_1_out_2));
  Multiplexer #(.width(6), .disabled(0), .enable("false")) multiplexer_1 (
    .in0(adder_1_out), .in1(multiplicar_x2_1_out_2), .out(out_4), .sel(comparador_ca2_1_out_3));
  Comparador_CA2 comparador_ca2_1 (.in_1(A), .in_2(adder_3_out), .out_3(comparador_ca2_1_out_3));  // open: out_5, out_4

  // Other names for the same wires on the sheet: Y[5:0] = out_4

  // Notes on the sheet:
  //   INPUTS
  //   IF THEN ELSE
  //   OUTPUT
endmodule

// Conv 4 a 6
module Conversor_4_a_6 (
  input  [3:0] in_1,
  output [5:0] out_2
);


  assign out_2 = {{3{in_1[3]}}, in_1[2:0]};
endmodule

// Neg 6BIT
module Conversor_a_Negativo (
  input  [5:0] in_1,
  output [5:0] out_2
);

  wire [5:0] not_1_out;

  Adder #(.width(6)) adder_1 (.a(6'b000001), .b(not_1_out), .out(out_2));  // open: cin, cout
  assign not_1_out = ~in_1;  // NOT_Gate not_1, 6 bits wide
endmodule

// Comparador CA2 6BIT
module Comparador_CA2 (
  input  [5:0] in_1,
  input  [5:0] in_2,
  output out_3,
  output out_4,
  output out_5
);

  Comparator #(.width(6), .mode("unsigned")) comparator_1 (
    .a({in_2[5], in_1[4:0]}), .b({in_1[5], in_2[4:0]}), .gt(out_3), .eq(out_4), .lt(out_5));
endmodule

// x2 6BIT
module Multiplicar_x2 (
  input  [5:0] in_1,
  output [5:0] out_2
);


  assign out_2 = {in_1[4:0], 1'b0};
endmodule
