// Logisim project PD2.circ as structural Verilog: 2 circuits, main circuit main
module main (
  input  [3:0] in_1,
  output [3:0] out_2
);

  wire and_2_out, CL, comparadorca2_1_out_3, comparadorca2_2_out_5, RST2, RSTA;
  wire [2:0] Iters;
  wire [3:0] A, counter_2_q;

  Clock clock_1 (.out(CL));
  Register #(.width(4)) register_1 (.D(in_1), .en(RSTA), .Q(A), .clk(CL));  // open: clr
  Counter #(.width(3), .max('h7)) counter_1 (.Q(Iters), .carry(RST2), .clk(CL));  // open: load, D, count, clr
  ComparadorCA2 comparadorca2_1 (.in_1(in_1), .in_2(4'b1011), .out_3(comparadorca2_1_out_3));  // open: out_4, out_5
  ComparadorCA2 comparadorca2_2 (.in_1(in_1), .in_2(A), .out_5(comparadorca2_2_out_5));  // open: out_3, out_4
  and and_1 (RSTA, ~Iters[0], ~Iters[1], ~Iters[2]);  // AND_Gate
  and and_2 (and_2_out, comparadorca2_1_out_3, comparadorca2_2_out_5, ~RSTA);  // AND_Gate
  Counter #(.width(4), .max('hf)) counter_2 (
    .count(and_2_out), .Q(counter_2_q), .clk(CL), .clr(RSTA));  // open: load, D, carry
  Multiplexer #(.width(4), .disabled(0), .enable("false")) multiplexer_1 (
    .in0(4'b0000), .in1(counter_2_q), .out(out_2), .sel(RST2));

  // Other names for the same wires on the sheet: X[3:0] = in_1

  // Notes on the sheet:
  //   INPUTS
  //   OPERACION
  //   X>(-5)
  //   A>X
  //   Si el ciclo es 0 almaceno X
  //   CICLOS
  //   Muestro el resultado en el ciclo 7
endmodule

module ComparadorCA2 (
  input  [3:0] in_1,
  input  [3:0] in_2,
  output out_3,
  output out_4,
  output out_5
);

  Comparator #(.width(4), .mode("unsigned")) comparator_1 (
    .a({in_2[3], in_1[2:0]}), .b({in_1[3], in_2[2:0]}), .gt(out_3), .eq(out_4), .lt(out_5));
endmodule
